# Fritzing sketch wiring (saved by Fritzing 0.9.5d)

parts:
  Part1 = Arduino Nano (Rev3.0)
  S1 = Toggle Switch spdt [package=THT]
  J1 = Basic Servo

nets:
  GND: Part1.GND, S1.COM, J1.gnd
  N1: Part1.D2, S1.L2
  N2: Part1.D3, S1.L1
  N3: Part1.D9, J1.pulse
  5V: Part1.5V, J1.vcc

custom parts:
  Toggle Switch spdt: Toggle Switch single pole double throw
